// Digital circuit 4位寄存器可控带时钟.dig as structural Verilog
module \_4位寄存器可控带时钟  (
  input  \可写 ,
  input  \时钟 ,
  input  [3:0] \_4位输入 ,
  input  \可输出 ,
  output [7:0] \输出 ,
  output [7:0] debug_out
);

  Register #(.Bits(4)) \u_寄存器  (.D(\_4位输入 ), .C(\时钟 ), .en(\可写 ), .Q(debug_out[3:0]));
  assign \输出  = \可输出  ? debug_out : 8'bz;  // Driver driver_1
  // Pins of 4 and 8 bits meet at debug_out
  // Pins of 4 and 8 bits meet at \输出 

  // Notes on the sheet:
  //   4位寄存器
endmodule
