// Digital circuit 8bit_add.dig as structural Verilog
module _8bit_add (
  input  A0,
  input  B0,
  input  A1,
  input  B1,
  input  A2,
  input  B2,
  input  A3,
  input  B3,
  input  A4,
  input  B4,
  input  A5,
  input  B5,
  input  A6,
  input  B6,
  input  A7,
  input  B7,
  output \位0 ,
  output \位1 ,
  output \位3 ,
  output \位4 ,
  output \位5 ,
  output \位6 ,
  output \位7 ,
  output \位8 ,
  output \CF_进位 
);

  wire all_add_1_c_out, all_add_2_c_out, all_add_3_c_out, all_add_4_c_out, all_add_5_c_out, all_add_6_c_out,
       half_1_c;

  half half_1 (.B(A0), .A(B0), .SUM(\位0 ), .C(half_1_c));
  all_add all_add_1 (.A(A1), .B(B1), .C_in(half_1_c), .SUM(\位1 ), .C_out(all_add_1_c_out));
  all_add all_add_2 (.A(A2), .B(B2), .C_in(all_add_1_c_out), .SUM(\位3 ), .C_out(all_add_2_c_out));
  all_add all_add_3 (.A(A3), .B(B3), .C_in(all_add_2_c_out), .SUM(\位4 ), .C_out(all_add_3_c_out));
  all_add all_add_4 (.A(A4), .B(B4), .C_in(all_add_3_c_out), .SUM(\位5 ), .C_out(all_add_4_c_out));
  all_add all_add_5 (.A(A5), .B(B5), .C_in(all_add_4_c_out), .SUM(\位6 ), .C_out(all_add_5_c_out));
  all_add all_add_6 (.A(A6), .B(B6), .C_in(all_add_5_c_out), .SUM(\位7 ), .C_out(all_add_6_c_out));
  all_add all_add_7 (.A(A7), .B(B7), .C_in(all_add_6_c_out), .SUM(\位8 ), .C_out(\CF_进位 ));

  // Notes on the sheet:
  //   半加器
  //   全加器
endmodule
