// Digital circuit 8位ALU加法器.dig as structural Verilog
module \_8位ALU加法器  (
  input  [7:0] \输入1 ,
  input  [7:0] \输入2 ,
  input  \可输出 ,
  output C,
  output [7:0] debug_out,
  output [7:0] \输出 
);

  Add #(.Bits(8)) add_1 (.a(\输入1 ), .b(\输入2 ), .c_i(1'b0), .s(debug_out), .c_o(C));
  assign \输出  = \可输出  ? debug_out : 8'bz;  // Driver driver_1

  // Notes on the sheet:
  //   简化版ALU,只有加法
endmodule
