// Digital circuit 8位加法器.dig as structural Verilog
module \_8位加法器  (
  input  [7:0] \输入A ,
  input  [7:0] \输入B ,
  input  \首个进位控制 ,
  output [7:0] \输出 ,
  output \最高进位 
);

  wire all_add_1_c_out, all_add_2_c_out, all_add_3_c_out, all_add_4_c_out, all_add_5_c_out, all_add_6_c_out,
       all_add_7_c_out;

  all_add all_add_1 (.A(\输入A [0]), .B(\输入B [0]), .C_in(\首个进位控制 ), .SUM(\输出 [0]), .C_out(all_add_1_c_out));
  all_add all_add_2 (.A(\输入A [1]), .B(\输入B [1]), .C_in(all_add_1_c_out), .SUM(\输出 [1]), .C_out(all_add_2_c_out));
  all_add all_add_3 (.A(\输入A [2]), .B(\输入B [2]), .C_in(all_add_2_c_out), .SUM(\输出 [2]), .C_out(all_add_3_c_out));
  all_add all_add_4 (.A(\输入A [3]), .B(\输入B [3]), .C_in(all_add_3_c_out), .SUM(\输出 [3]), .C_out(all_add_4_c_out));
  all_add all_add_5 (.A(\输入A [4]), .B(\输入B [4]), .C_in(all_add_4_c_out), .SUM(\输出 [4]), .C_out(all_add_5_c_out));
  all_add all_add_6 (.A(\输入A [5]), .B(\输入B [5]), .C_in(all_add_5_c_out), .SUM(\输出 [5]), .C_out(all_add_6_c_out));
  all_add all_add_7 (.A(\输入A [6]), .B(\输入B [6]), .C_in(all_add_6_c_out), .SUM(\输出 [6]), .C_out(all_add_7_c_out));
  all_add all_add_8 (.A(\输入A [7]), .B(\输入B [7]), .C_in(all_add_7_c_out), .SUM(\输出 [7]), .C_out(\最高进位 ));
endmodule
