// Digital circuit 8位取反器.dig as structural Verilog
module \_8位取反器  (
  input  \开启取反 ,
  input  [7:0] \_8位输入 ,
  output [7:0] \输出8位 
);

  \取反  \u_取反_1  (.\是否取反 (\开启取反 ), .\输入 (\_8位输入 [0]), .\输出 (\输出8位 [0]));
  \取反  \u_取反_2  (.\是否取反 (\开启取反 ), .\输入 (\_8位输入 [1]), .\输出 (\输出8位 [1]));
  \取反  \u_取反_3  (.\是否取反 (\开启取反 ), .\输入 (\_8位输入 [2]), .\输出 (\输出8位 [2]));
  \取反  \u_取反_4  (.\是否取反 (\开启取反 ), .\输入 (\_8位输入 [3]), .\输出 (\输出8位 [3]));
  \取反  \u_取反_5  (.\是否取反 (\开启取反 ), .\输入 (\_8位输入 [4]), .\输出 (\输出8位 [4]));
  \取反  \u_取反_6  (.\是否取反 (\开启取反 ), .\输入 (\_8位输入 [5]), .\输出 (\输出8位 [5]));
  \取反  \u_取反_7  (.\是否取反 (\开启取反 ), .\输入 (\_8位输入 [6]), .\输出 (\输出8位 [6]));
  \取反  \u_取反_8  (.\是否取反 (\开启取反 ), .\输入 (\_8位输入 [7]), .\输出 (\输出8位 [7]));
endmodule
