// Digital circuit 8位寄存器.dig as structural Verilog
module \_8位寄存器  (
  input  \可写 ,
  input  \时钟 ,
  input  [7:0] \_8位输入 ,
  input  \可输出 ,
  output [7:0] \输出 ,
  output [7:0] debug_out
);

  Register #(.Bits(8)) \u_寄存器  (.D(\_8位输入 ), .C(\时钟 ), .en(\可写 ), .Q(debug_out));
  assign \输出  = \可输出  ? debug_out : 8'bz;  // Driver driver_1
endmodule
