// Digital circuit add_and_sub.dig as structural Verilog
module add_and_sub (
  input  [7:0] \输入1 ,
  input  [7:0] \输入2 ,
  input  \负数控制 ,
  output [7:0] \输出结果 ,
  output \进位 
);

  wire \_8位加法器_1_最高进位 , not_1_out;
  wire [7:0] \_8位取反器_1_输出8位 ;

  not not_1 (not_1_out, \负数控制 );
  \_8位取反器  \_8位取反器_1  (.\开启取反 (\负数控制 ), .\_8位输入 (\输入2 ), .\输出8位 (\_8位取反器_1_输出8位 ));
  \_8位加法器  \_8位加法器_1  (
    .\输入A (\_8位取反器_1_输出8位 ), .\输入B (\输入1 ), .\首个进位控制 (\负数控制 ), .\输出 (\输出结果 ), .\最高进位 (\_8位加法器_1_最高进位 ));
  and and_1 (\进位 , \_8位加法器_1_最高进位 , not_1_out);

  // Notes on the sheet:
  //   非门
  //   与门
endmodule
