// Digital circuit all add.dig as structural Verilog
module all_add (
  input  A,
  input  B,
  input  C_in,
  output SUM,
  output C_out
);

  wire half_1_c, half_1_sum, half_2_c;

  half half_1 (.B(A), .A(B), .SUM(half_1_sum), .C(half_1_c));
  half half_2 (.B(C_in), .A(half_1_sum), .SUM(SUM), .C(half_2_c));
  or or_1 (C_out, half_2_c, half_1_c);

  // Notes on the sheet:
  //   输入电信号1或0
  //   接受输入的进位(1或0)
  //   半加器
  //   或门
  //   相加结果
  //   输出的进位(1或0)
endmodule
