// Digital circuit and gate.dig as structural Verilog
module and_gate (
  input  A,
  input  in_2,
  output out_3
);

  wire relaydt_1_p4;

  // RelayDT relaydt_1: pin names not known; wires that end beside it: A, 1'b1, 1'b0, relaydt_1_p4
  // RelayDT relaydt_2: pin names not known; wires that end beside it: in_2, relaydt_1_p4, 1'b0, out_3
endmodule
