// Digital circuit bus_error.dig as structural Verilog
module bus_error (
  input  \输入 ,
  input  WriteEnable,
  input  \是否能输出 ,
  input  \输入_2 ,
  input  WriteEnable_2,
  input  \是否能输出_2 
);

  wire lock_1_out, lock_2_out, relaydt_1_p5;

  lock lock_1 (.\数据输入 (\输入 ), .Write_Enable(WriteEnable), .out(lock_1_out));
  lock lock_2 (.\数据输入 (\输入_2 ), .Write_Enable(WriteEnable_2), .out(lock_2_out));
  // RelayDT relaydt_1: pin names not known; wires that end beside it: \是否能输出 , lock_1_out, \是否能输出_2 , 1'b0, relaydt_1_p5, 1'b0, relaydt_1_p5
  // RelayDT relaydt_2: pin names not known; wires that end beside it: lock_2_out, relaydt_1_p5, relaydt_1_p5

  // Notes on the sheet:
  //   假装的总线
endmodule
