// Digital circuit half.dig as structural Verilog
module half (
  input  B,
  input  A,
  output SUM,
  output C
);

  xor xor_1 (SUM, A, B);
  and and_1 (C, A, B);

  // Notes on the sheet:
  //   电信号1或0
  //   与门
  //   异或门
  //   A+B的结果
  //   进位
endmodule
