// Digital circuit lock.dig as structural Verilog
module lock (
  input  \数据输入 ,
  input  Write_Enable,
  output out
);

  wire and_1_out, and_2_out, not_1_out, not_2_out, or_1_out;

  and and_1 (and_1_out, \数据输入 , Write_Enable);
  not not_1 (not_1_out, \数据输入 );
  and and_2 (and_2_out, not_1_out, Write_Enable);
  or or_1 (or_1_out, out, and_1_out);
  not not_2 (not_2_out, and_2_out);
  and and_3 (out, or_1_out, not_2_out);

  // Notes on the sheet:
  //   锁存器
  //   与门
  //   非门
  //   或门
endmodule
