// Digital circuit mem_ceil.dig as structural Verilog
module mem_ceil (
  input  \是否能输出_LD ,
  input  \数据输入 ,
  input  \可写控制_store ,
  input  \列 ,
  input  \行 ,
  output \结果 
);

  wire and_1_out, and_2_out, and_3_out, lock_1_out;

  and and_1 (and_1_out, \列 , \行 );
  and and_2 (and_2_out, \是否能输出_LD , and_1_out);
  and and_3 (and_3_out, \可写控制_store , and_1_out);
  lock lock_1 (.\数据输入 (\数据输入 ), .Write_Enable(and_3_out), .out(lock_1_out));
  assign \结果  = and_2_out ? lock_1_out : 1'bz;  // Driver driver_1

  // Notes on the sheet:
  //   一个内存单元
endmodule
