// Digital circuit memery.dig as structural Verilog
module memery (
  input  \输入数据 ,
  input  \可写_store ,
  input  LD,
  input  [3:0] \输入地址 ,
  output \输出 
);

  wire [7:0] \地址表_out ;

  LookUpTable #(.Bits(8)) \u_地址表  (.in0(\输入地址 [0]), .in1(\输入地址 [1]), .in2(\输入地址 [2]), .in3(\输入地址 [3]), .out(\地址表_out ));
  mem_ceil mem_ceil_1 (
    .\是否能输出_LD (LD), .\数据输入 (\输入数据 ), .\可写控制_store (\可写_store ), .\列 (\地址表_out [1]), .\行 (\地址表_out [0]),
    .\结果 (\输出 ));
  mem_ceil mem_ceil_2 (
    .\是否能输出_LD (LD), .\数据输入 (\输入数据 ), .\可写控制_store (\可写_store ), .\列 (\地址表_out [1]), .\行 (\地址表_out [2]),
    .\结果 (\输出 ));
  mem_ceil mem_ceil_3 (
    .\是否能输出_LD (LD), .\数据输入 (\输入数据 ), .\可写控制_store (\可写_store ), .\列 (\地址表_out [1]), .\行 (\地址表_out [4]),
    .\结果 (\输出 ));
  mem_ceil mem_ceil_4 (
    .\是否能输出_LD (LD), .\数据输入 (\输入数据 ), .\可写控制_store (\可写_store ), .\列 (\地址表_out [1]), .\行 (\地址表_out [6]),
    .\结果 (\输出 ));
  mem_ceil mem_ceil_5 (
    .\是否能输出_LD (LD), .\数据输入 (\输入数据 ), .\可写控制_store (\可写_store ), .\列 (\地址表_out [3]), .\行 (\地址表_out [0]),
    .\结果 (\输出 ));
  mem_ceil mem_ceil_6 (
    .\是否能输出_LD (LD), .\数据输入 (\输入数据 ), .\可写控制_store (\可写_store ), .\列 (\地址表_out [3]), .\行 (\地址表_out [2]),
    .\结果 (\输出 ));
  mem_ceil mem_ceil_7 (
    .\是否能输出_LD (LD), .\数据输入 (\输入数据 ), .\可写控制_store (\可写_store ), .\列 (\地址表_out [3]), .\行 (\地址表_out [4]),
    .\结果 (\输出 ));
  mem_ceil mem_ceil_8 (
    .\是否能输出_LD (LD), .\数据输入 (\输入数据 ), .\可写控制_store (\可写_store ), .\列 (\地址表_out [3]), .\行 (\地址表_out [6]),
    .\结果 (\输出 ));
  mem_ceil mem_ceil_9 (
    .\是否能输出_LD (LD), .\数据输入 (\输入数据 ), .\可写控制_store (\可写_store ), .\列 (\地址表_out [5]), .\行 (\地址表_out [0]),
    .\结果 (\输出 ));
  mem_ceil mem_ceil_10 (
    .\是否能输出_LD (LD), .\数据输入 (\输入数据 ), .\可写控制_store (\可写_store ), .\列 (\地址表_out [5]), .\行 (\地址表_out [2]),
    .\结果 (\输出 ));
  mem_ceil mem_ceil_11 (
    .\是否能输出_LD (LD), .\数据输入 (\输入数据 ), .\可写控制_store (\可写_store ), .\列 (\地址表_out [5]), .\行 (\地址表_out [4]),
    .\结果 (\输出 ));
  mem_ceil mem_ceil_12 (
    .\是否能输出_LD (LD), .\数据输入 (\输入数据 ), .\可写控制_store (\可写_store ), .\列 (\地址表_out [5]), .\行 (\地址表_out [6]),
    .\结果 (\输出 ));
  mem_ceil mem_ceil_13 (
    .\是否能输出_LD (LD), .\数据输入 (\输入数据 ), .\可写控制_store (\可写_store ), .\列 (\地址表_out [7]), .\行 (\地址表_out [0]),
    .\结果 (\输出 ));
  mem_ceil mem_ceil_14 (
    .\是否能输出_LD (LD), .\数据输入 (\输入数据 ), .\可写控制_store (\可写_store ), .\列 (\地址表_out [7]), .\行 (\地址表_out [2]),
    .\结果 (\输出 ));
  mem_ceil mem_ceil_15 (
    .\是否能输出_LD (LD), .\数据输入 (\输入数据 ), .\可写控制_store (\可写_store ), .\列 (\地址表_out [7]), .\行 (\地址表_out [4]),
    .\结果 (\输出 ));
  mem_ceil mem_ceil_16 (
    .\是否能输出_LD (LD), .\数据输入 (\输入数据 ), .\可写控制_store (\可写_store ), .\列 (\地址表_out [7]), .\行 (\地址表_out [6]),
    .\结果 (\输出 ));

  // Notes on the sheet:
  //   contents of 地址表 (hex, n*v repeats v):
  //   3,9,21,81,6,c,24,84,12,18,30,90,42,48,60,c0
endmodule
