// Digital circuit memery1.dig as structural Verilog
module memery1 (
  input  \输入数据 ,
  input  \可写_store ,
  input  LD,
  input  \行1 ,
  input  \行2 ,
  input  \行3 ,
  input  \列1 ,
  input  \列2 ,
  input  \列3 ,
  input  \列4 ,
  input  \行4 ,
  output \输出 
);

  mem_ceil mem_ceil_1 (
    .\是否能输出_LD (LD), .\数据输入 (\输入数据 ), .\可写控制_store (\可写_store ), .\列 (\列1 ), .\行 (\行1 ), .\结果 (\输出 ));
  mem_ceil mem_ceil_2 (
    .\是否能输出_LD (LD), .\数据输入 (\输入数据 ), .\可写控制_store (\可写_store ), .\列 (\列1 ), .\行 (\行2 ), .\结果 (\输出 ));
  mem_ceil mem_ceil_3 (
    .\是否能输出_LD (LD), .\数据输入 (\输入数据 ), .\可写控制_store (\可写_store ), .\列 (\列1 ), .\行 (\行3 ), .\结果 (\输出 ));
  mem_ceil mem_ceil_4 (
    .\是否能输出_LD (LD), .\数据输入 (\输入数据 ), .\可写控制_store (\可写_store ), .\列 (\列1 ), .\行 (\行4 ), .\结果 (\输出 ));
  mem_ceil mem_ceil_5 (
    .\是否能输出_LD (LD), .\数据输入 (\输入数据 ), .\可写控制_store (\可写_store ), .\列 (\列2 ), .\行 (\行1 ), .\结果 (\输出 ));
  mem_ceil mem_ceil_6 (
    .\是否能输出_LD (LD), .\数据输入 (\输入数据 ), .\可写控制_store (\可写_store ), .\列 (\列2 ), .\行 (\行2 ), .\结果 (\输出 ));
  mem_ceil mem_ceil_7 (
    .\是否能输出_LD (LD), .\数据输入 (\输入数据 ), .\可写控制_store (\可写_store ), .\列 (\列2 ), .\行 (\行3 ), .\结果 (\输出 ));
  mem_ceil mem_ceil_8 (
    .\是否能输出_LD (LD), .\数据输入 (\输入数据 ), .\可写控制_store (\可写_store ), .\列 (\列2 ), .\行 (\行4 ), .\结果 (\输出 ));
  mem_ceil mem_ceil_9 (
    .\是否能输出_LD (LD), .\数据输入 (\输入数据 ), .\可写控制_store (\可写_store ), .\列 (\列3 ), .\行 (\行1 ), .\结果 (\输出 ));
  mem_ceil mem_ceil_10 (
    .\是否能输出_LD (LD), .\数据输入 (\输入数据 ), .\可写控制_store (\可写_store ), .\列 (\列3 ), .\行 (\行2 ), .\结果 (\输出 ));
  mem_ceil mem_ceil_11 (
    .\是否能输出_LD (LD), .\数据输入 (\输入数据 ), .\可写控制_store (\可写_store ), .\列 (\列3 ), .\行 (\行3 ), .\结果 (\输出 ));
  mem_ceil mem_ceil_12 (
    .\是否能输出_LD (LD), .\数据输入 (\输入数据 ), .\可写控制_store (\可写_store ), .\列 (\列3 ), .\行 (\行4 ), .\结果 (\输出 ));
  mem_ceil mem_ceil_13 (
    .\是否能输出_LD (LD), .\数据输入 (\输入数据 ), .\可写控制_store (\可写_store ), .\列 (\列4 ), .\行 (\行1 ), .\结果 (\输出 ));
  mem_ceil mem_ceil_14 (
    .\是否能输出_LD (LD), .\数据输入 (\输入数据 ), .\可写控制_store (\可写_store ), .\列 (\列4 ), .\行 (\行2 ), .\结果 (\输出 ));
  mem_ceil mem_ceil_15 (
    .\是否能输出_LD (LD), .\数据输入 (\输入数据 ), .\可写控制_store (\可写_store ), .\列 (\列4 ), .\行 (\行3 ), .\结果 (\输出 ));
  mem_ceil mem_ceil_16 (
    .\是否能输出_LD (LD), .\数据输入 (\输入数据 ), .\可写控制_store (\可写_store ), .\列 (\列4 ), .\行 (\行4 ), .\结果 (\输出 ));
endmodule
