// Digital circuit not gate.dig as structural Verilog
module not_gate (
  input  A,
  output out_2
);

  // RelayDT relaydt_1: pin names not known; wires that end beside it: A, 1'b1, 1'b0, out_2
endmodule
