// Digital circuit or gate.dig as structural Verilog
module or_gate (
  input  in_1,
  input  in_2,
  output out_3
);

  // RelayDT relaydt_1: pin names not known; wires that end beside it: in_1, 1'b1, in_2, 1'b0, out_3, 1'b0
  // RelayDT relaydt_2: pin names not known; wires that end beside it: 1'b1, out_3
endmodule
