// Digital circuit register.dig as structural Verilog
module register (
  input  WriteEnable,
  input  [7:0] \输入8位数据 ,
  output [7:0] out_1
);

  lock lock_1 (.\数据输入 (\输入8位数据 [0]), .Write_Enable(WriteEnable), .out(out_1[0]));
  lock lock_2 (.\数据输入 (\输入8位数据 [1]), .Write_Enable(WriteEnable), .out(out_1[1]));
  lock lock_3 (.\数据输入 (\输入8位数据 [2]), .Write_Enable(WriteEnable), .out(out_1[2]));
  lock lock_4 (.\数据输入 (\输入8位数据 [3]), .Write_Enable(WriteEnable), .out(out_1[3]));
  lock lock_5 (.\数据输入 (\输入8位数据 [4]), .Write_Enable(WriteEnable), .out(out_1[4]));
  lock lock_6 (.\数据输入 (\输入8位数据 [5]), .Write_Enable(WriteEnable), .out(out_1[5]));
  lock lock_7 (.\数据输入 (\输入8位数据 [6]), .Write_Enable(WriteEnable), .out(out_1[6]));
  lock lock_8 (.\数据输入 (\输入8位数据 [7]), .Write_Enable(WriteEnable), .out(out_1[7]));

  // Notes on the sheet:
  //   控制写入,8根线由1个控制器控制
  //   寄存器的实现
  //   8个锁存器
  //   输出8位
  //   分裂器,能把多个线合并的东西,输入8个1位
  //   输出8位2进制
endmodule
