// Digital circuit xor gate.dig as structural Verilog
module xor_gate (
  input  in_1,
  input  in_2,
  output out_3
);

  wire relaydt_1_p2, relaydt_1_p3;

  // RelayDT relaydt_1: pin names not known; wires that end beside it: 1'b1, relaydt_1_p2, relaydt_1_p3
  // RelayDT relaydt_2: pin names not known; wires that end beside it: in_1, 1'b0, in_2, relaydt_1_p3, relaydt_1_p2, 1'b0, out_3
endmodule
