// Digital circuit xor my.dig as structural Verilog
module xor_my (
  input  \输入1 ,
  input  \输入2 ,
  output out_3
);

  wire and_1_out, and_2_out, not_1_out, not_2_out;

  not not_1 (not_1_out, \输入2 );
  not not_2 (not_2_out, \输入1 );
  and and_1 (and_1_out, \输入1 , not_1_out);
  and and_2 (and_2_out, not_2_out, \输入2 );
  or or_1 (out_3, and_1_out, and_2_out);
endmodule
