// Digital circuit 带时钟的锁存器.dig as structural Verilog
module \带时钟的锁存器  (
  input  \输入 ,
  output out_2
);

  wire lock_1_out, not_1_out, \假装的时钟_out ;

  Button \u_假装的时钟  (.out(\假装的时钟_out ));
  not not_1 (not_1_out, \假装的时钟_out );
  lock lock_1 (.\数据输入 (\输入 ), .Write_Enable(\假装的时钟_out ), .out(lock_1_out));
  lock lock_2 (.\数据输入 (lock_1_out), .Write_Enable(not_1_out), .out(out_2));
endmodule
