// Digital circuit 带时钟的锁存器最终版本.dig as structural Verilog
module \带时钟的锁存器最终版本  (
  input  \输入 ,
  input  \可写_WriteEnable ,
  output \输出 
);

  wire and_1_out, not_1_out, \假装时钟_out , \锁存器_out ;

  Button \u_假装时钟  (.out(\假装时钟_out ));
  and and_1 (and_1_out, \可写_WriteEnable , \假装时钟_out );
  lock \u_锁存器  (.\数据输入 (\输入 ), .Write_Enable(and_1_out), .out(\锁存器_out ));
  not not_1 (not_1_out, \假装时钟_out );
  lock lock_1 (.\数据输入 (\锁存器_out ), .Write_Enable(not_1_out), .out(\输出 ));

  // Notes on the sheet:
  //   这里的输出有可能是前一次的值
  //   这里的输出一定是正确的
endmodule
