// Digital circuit 带输出控制的寄存器.dig as structural Verilog
module \带输出控制的寄存器  (
  input  WriteEnable,
  input  [7:0] \输入8位数据 ,
  input  \是否输出 ,
  output [7:0] out_3
);

  wire lock_1_out, lock_2_out, lock_3_out, lock_4_out, lock_5_out, lock_6_out, lock_7_out, lock_8_out;

  assign out_3[0] = \是否输出  ? lock_1_out : 1'bz;  // Driver driver_1
  lock lock_1 (.\数据输入 (\输入8位数据 [0]), .Write_Enable(WriteEnable), .out(lock_1_out));
  lock lock_2 (.\数据输入 (\输入8位数据 [1]), .Write_Enable(WriteEnable), .out(lock_2_out));
  assign out_3[1] = \是否输出  ? lock_2_out : 1'bz;  // Driver driver_2
  assign out_3[2] = \是否输出  ? lock_3_out : 1'bz;  // Driver driver_3
  lock lock_3 (.\数据输入 (\输入8位数据 [2]), .Write_Enable(WriteEnable), .out(lock_3_out));
  assign out_3[3] = \是否输出  ? lock_4_out : 1'bz;  // Driver driver_4
  lock lock_4 (.\数据输入 (\输入8位数据 [3]), .Write_Enable(WriteEnable), .out(lock_4_out));
  assign out_3[4] = \是否输出  ? lock_5_out : 1'bz;  // Driver driver_5
  lock lock_5 (.\数据输入 (\输入8位数据 [4]), .Write_Enable(WriteEnable), .out(lock_5_out));
  lock lock_6 (.\数据输入 (\输入8位数据 [5]), .Write_Enable(WriteEnable), .out(lock_6_out));
  assign out_3[5] = \是否输出  ? lock_6_out : 1'bz;  // Driver driver_6
  assign out_3[6] = \是否输出  ? lock_7_out : 1'bz;  // Driver driver_7
  lock lock_7 (.\数据输入 (\输入8位数据 [6]), .Write_Enable(WriteEnable), .out(lock_7_out));
  assign out_3[7] = \是否输出  ? lock_8_out : 1'bz;  // Driver driver_8
  lock lock_8 (.\数据输入 (\输入8位数据 [7]), .Write_Enable(WriteEnable), .out(lock_8_out));

  // Notes on the sheet:
  //   8个锁存器
  //   输出8位
endmodule
